# Fritzing sketch bokinbako pcb rev2 (saved by Fritzing 0.9.3b)
circuit board: 5.3cm x 6.05cm
breadboards: 1

parts:
  part = Piezo Speaker
  part_2 = female pin header, 3 pins [form="♀ (female)"]
  part_3 = female pin header, 2 pins [form="♀ (female)"]
  SW = Toggle Switch [package=THT]
  part_4 = Arduino Nano (Rev3.0)
  part_5 = seeeduino-xiao
  part_6 = female pin header, 4 pins [form="♀ (female)"]
  part_7 = Power plug
  part_8 = RELAY-2 [package=relay-g5v]

nets (from the pcb view):
  N1: part.pin1, part_4.D4
  GND: part.pin2, part_2.pin1, part_3.pin2, part_4.GND, part_5.D1, part_5.GND, part_6.pin4, part_7.GND, part_8.9
  N2: part_2.pin2, part_5.D5
  N3: part_2.pin3, part_3.pin1, part_8.1
  VIN: SW.L1, part_4.VIN, part_5.5V
  N4: SW.COM, part_7.VCC, part_8.6
  N5: part_4.D2, part_6.pin3
  N6: part_4.D3, part_8.2
  N7: part_4.D5, part_6.pin2
  N8: part_4.5V, part_6.pin1

notes:
  DC 5V
  SPK
  LED PNL
  ULTRASONIC
  Ctrl
  LED
  R  G  W
  G  E  T  V
  LED TAG
  LED　Bokinbako V1 Rev.2

custom parts:
  seeeduino-xiao: Seeeduino XIAO processor board.
